// Logisim project control-logic.circ as structural Verilog: 1 circuit, main circuit control_logic
module control_logic (
  input  [31:0] Instruction,
  input  BrEq,
  input  BrLt,
  output PCSel,
  output RegWEn,
  output [2:0] ImmSel,
  output BrUn,
  output ASel,
  output BSel,
  output [3:0] ALUSel,
  output MemWEn,
  output [1:0] WBSel
);

  wire and_27_out, and_28_out, and_29_out, B_type, func3_0, func3_1, func3_2, func3_3, func3_4, func3_5,
       func3_6, func3_7, I_type, is_add, is_addi, is_and, is_andi, is_beq, is_bge, is_bgeu, is_blt, is_bltu,
       is_bne, is_mul, is_mulh, is_mulhu, is_or, is_ori, is_sll, is_slli, is_slt, is_slti, is_sra, is_srai,
       is_srl, is_srli, is_sub, is_xor, is_xori, nor_1_out, not_1_out, not_2_out, not_3_out, not_4_out,
       not_5_out, not_6_out, not_7_out, R_type;
  wire [2:0] priority_encoder_1_out;
  wire [5:0] ROM_Input;
  wire [15:14] rom_1_data;

  Comparator #(.width(3)) comparator_1 (.a(Instruction[14:12]), .b(3'b110), .eq(func3_6));  // open: gt, lt
  Comparator #(.width(3)) comparator_2 (.a(Instruction[14:12]), .b(3'b011), .eq(func3_3));  // open: gt, lt
  Comparator #(.width(5)) comparator_3 (.a(Instruction[6:2]), .b(5'b00100), .eq(I_type));  // open: gt, lt
  Comparator #(.width(5)) comparator_4 (.a(Instruction[6:2]), .b(5'b01100), .eq(R_type));  // open: gt, lt
  Comparator #(.width(5)) comparator_5 (.a(Instruction[6:2]), .b(5'b11000), .eq(B_type));  // open: gt, lt
  Comparator #(.width(3)) comparator_6 (.a(Instruction[14:12]), .b(3'b000), .eq(func3_0));  // open: gt, lt
  Comparator #(.width(3)) comparator_7 (.a(Instruction[14:12]), .b(3'b111), .eq(func3_7));  // open: gt, lt
  Comparator #(.width(3)) comparator_8 (.a(Instruction[14:12]), .b(3'b101), .eq(func3_5));  // open: gt, lt
  Comparator #(.width(3)) comparator_9 (.a(Instruction[14:12]), .b(3'b001), .eq(func3_1));  // open: gt, lt
  Comparator #(.width(3)) comparator_10 (.a(Instruction[14:12]), .b(3'b010), .eq(func3_2));  // open: gt, lt
  Comparator #(.width(3)) comparator_11 (.a(Instruction[14:12]), .b(3'b100), .eq(func3_4));  // open: gt, lt
  ROM #(.addrWidth(6), .dataWidth(16)) rom_1 (
    .addr(ROM_Input), .data({rom_1_data, WBSel, MemWEn, ALUSel, BSel, ASel, BrUn, ImmSel, RegWEn}));
  not not_1 (not_1_out, Instruction[30]);
  not not_2 (not_2_out, Instruction[30]);
  not not_3 (not_3_out, Instruction[30]);
  and and_1 (is_addi, I_type, func3_0);
  and and_2 (is_andi, I_type, func3_7);
  and and_3 (is_ori, I_type, func3_6);
  and and_4 (is_xori, I_type, func3_4);
  and and_5 (is_slli, I_type, func3_1);
  and and_6 (is_srli, I_type, not_1_out, func3_5);
  and and_7 (is_srai, I_type, Instruction[30], func3_5);
  and and_8 (is_slti, I_type, func3_2);
  and and_9 (is_add, R_type, not_2_out, func3_0);
  and and_10 (is_sub, R_type, Instruction[30], func3_0);
  and and_11 (is_and, R_type, func3_7);
  and and_12 (is_or, R_type, func3_6);
  and and_13 (is_xor, R_type, func3_4);
  and and_14 (is_sll, R_type, func3_1);
  and and_15 (is_srl, R_type, not_3_out, func3_5);
  and and_16 (is_sra, R_type, Instruction[30], func3_5);
  and and_17 (is_slt, R_type, func3_2);
  and and_18 (is_mul, R_type, Instruction[25], func3_0);
  and and_19 (is_mulh, R_type, Instruction[25], func3_1);
  and and_20 (is_mulhu, R_type, Instruction[25], func3_3);
  and and_21 (is_beq, B_type, func3_0);
  and and_22 (is_bge, B_type, func3_5);
  and and_23 (is_bgeu, B_type, func3_7);
  and and_24 (is_blt, B_type, func3_4);
  and and_25 (is_bltu, B_type, func3_6);
  and and_26 (is_bne, B_type, func3_1);
  or or_1 (BrUn, is_bgeu, is_bltu);
  not not_4 (not_4_out, B_type);
  Priority_Encoder priority_encoder_1 (
    .in0(not_4_out), .in1(is_beq), .in2(is_bge), .in3(is_bgeu), .in4(is_blt), .in5(is_bltu), .in6(is_bne),
    .out(priority_encoder_1_out));  // open: in7, en_in, gs, en_out
  Priority_Encoder #(.select_enc(6)) priority_encoder_2 (
    .in0(is_addi), .in1(is_andi), .in2(is_ori), .in3(is_xori), .in4(is_slli), .in5(is_srli), .in6(is_srai),
    .in7(is_slti), .in8(is_add), .in9(is_sub), .in10(is_and), .in11(is_or), .in12(is_xor), .in13(is_sll),
    .in14(is_srl), .in15(is_sra), .in16(is_slt), .in17(is_mul), .in18(is_mulh), .in19(is_mulhu),
    .in20(is_beq), .in21(is_bge), .in22(is_bgeu), .in23(is_blt), .in24(is_bltu), .in25(is_bne),
    .out(ROM_Input));  // open: in26, in27, in28, in29, in30, in31, in32, in33, in34, in35, in36, in37, in38, in39, in40, in41, in42, in43, in44, in45, in46, in47, in48, in49, in50, in51, in52, in53, in54, in55, in56, in57, in58, in59, in60, in61, in62, in63, gs, en_out, en_in
  not not_5 (not_5_out, BrUn);
  not not_6 (not_6_out, BrLt);
  and and_27 (and_27_out, not_6_out, BrUn);
  and and_28 (and_28_out, BrLt, BrUn);
  not not_7 (not_7_out, BrEq);
  nor nor_1 (nor_1_out, BrLt, BrUn);
  and and_29 (and_29_out, BrLt, not_5_out);
  Multiplexer #(.select(3)) multiplexer_1 (
    .in0(1'b0), .in1(BrEq), .in2(nor_1_out), .in3(and_27_out), .in4(and_29_out), .in5(and_28_out),
    .in6(not_7_out), .in7(1'b1), .out(PCSel), .sel(priority_encoder_1_out));

  // Other names for the same wires on the sheet: opcode[4:0] = Instruction[6:2]; funct3[2:0] = Instruction[14:12];
  //   mulType = Instruction[25]; alter = Instruction[30]

  // Notes on the sheet:
  //   INPUTS to your circuit
  //   contents of rom_1 (hex, n*v repeats v):
  //   1041 13c1 1341 1241 10c1 12c1 16c1 1141 1001 1601 1381 1301 1201 1081 1281 1681 1101 1401 1481 1581
  //   64 64 74 64 74 64
  //   ROM FOR CONTROL LOGIC
  //   DON'T CHANGE THE LOCATIONS OF THE INPUTS AND OUTPUTS!
  //   This is only if you choose to do the ROM option
  //   OUTPUT from your circuit
endmodule
