// Logisim project cpu.circ as structural Verilog: 1 circuit, main circuit cpu
module cpu (
  input  clk,
  input  [31:0] Instruction,
  input  [31:0] MemReadData,
  output [31:0] MemAddress,
  output [31:0] ProgramCounter,
  output [31:0] ra,
  output [31:0] sp,
  output [31:0] t0,
  output [31:0] t1,
  output [31:0] t2,
  output [31:0] s0,
  output [31:0] s1,
  output [31:0] a0,
  output [3:0] MemWriteMask,
  output [31:0] MemWriteData
);

  wire branch_comp_1_breq, branch_comp_1_brlt, control_logic_1_asel, control_logic_1_brun,
       control_logic_1_bsel, control_logic_1_memwen, control_logic_1_pcsel, control_logic_1_regwen;
  wire [1:0] control_logic_1_wbsel;
  wire [2:0] control_logic_1_immsel;
  wire [3:0] control_logic_1_alusel;
  wire [31:0] adder_1_out, Data2Reg, DataFromReg, imm_gen_1_immediate, multiplexer_1_out, multiplexer_2_out,
       multiplexer_3_out, multiplexer_4_out, PC_Plus_4, regfile_1_readdata1, register_1_q;

  Adder #(.width(32)) adder_1 (.a(register_1_q), .b(32'h1), .out(adder_1_out));  // open: cin, cout
  Adder #(.width(32)) adder_2 (.a(ProgramCounter), .b(32'h4), .out(PC_Plus_4));  // open: cin, cout
  Register #(.width(32)) register_1 (.D(adder_1_out), .clk(clk), .Q(register_1_q));  // open: en, clr
  Multiplexer #(.width(32)) multiplexer_1 (
    .in0(PC_Plus_4), .in1(MemAddress), .out(multiplexer_1_out), .sel(control_logic_1_pcsel));
  // Probe on register_1_q
  Register #(.width(32)) PC (.D(multiplexer_1_out), .clk(clk), .Q(ProgramCounter));  // open: en, clr
  regfile regfile_1 (
    .ReadIndex1(Instruction[19:15]), .ReadIndex2(Instruction[24:20]), .WriteIndex(Instruction[11:7]),
    .WriteData(multiplexer_4_out), .RegWEn(control_logic_1_regwen), .clk(clk), .ra(ra), .sp(sp), .t0(t0),
    .t1(t1), .t2(t2), .s0(s0), .s1(s1), .a0(a0), .ReadData1(regfile_1_readdata1), .ReadData2(DataFromReg));
  imm_gen imm_gen_1 (.Instruction(Instruction), .ImmSel(control_logic_1_immsel), .Immediate(imm_gen_1_immediate));
  control_logic control_logic_1 (
    .Instruction(Instruction), .BrEq(branch_comp_1_breq), .BrLt(branch_comp_1_brlt),
    .PCSel(control_logic_1_pcsel), .RegWEn(control_logic_1_regwen), .ImmSel(control_logic_1_immsel),
    .BrUn(control_logic_1_brun), .ASel(control_logic_1_asel), .BSel(control_logic_1_bsel),
    .ALUSel(control_logic_1_alusel), .MemWEn(control_logic_1_memwen), .WBSel(control_logic_1_wbsel));
  Multiplexer #(.width(32)) multiplexer_2 (
    .in0(regfile_1_readdata1), .in1(ProgramCounter), .out(multiplexer_2_out), .sel(control_logic_1_asel));
  Multiplexer #(.width(32)) multiplexer_3 (
    .in0(DataFromReg), .in1(imm_gen_1_immediate), .out(multiplexer_3_out), .sel(control_logic_1_bsel));
  alu alu_1 (.A(multiplexer_2_out), .B(multiplexer_3_out), .ALUSel(control_logic_1_alusel), .ALUResult(MemAddress));
  branch_comp branch_comp_1 (
    .BrData1(regfile_1_readdata1), .BrData2(DataFromReg), .BrUn(control_logic_1_brun),
    .BrEq(branch_comp_1_breq), .BrLt(branch_comp_1_brlt));
  Multiplexer #(.select(2), .width(32)) multiplexer_4 (
    .in0(Data2Reg), .in1(MemAddress), .in2(PC_Plus_4), .out(multiplexer_4_out), .sel(control_logic_1_wbsel));  // open: in3
  partial_store partial_store_1 (
    .Instruction(Instruction), .MemAddress(MemAddress), .DataFromReg(DataFromReg),
    .MemWEn(control_logic_1_memwen), .MemWriteMask(MemWriteMask), .DataToMem(MemWriteData));
  partial_load partial_load_1 (
    .Instruction(Instruction), .MemAddress(MemAddress), .DataFromMem(MemReadData), .DataToReg(Data2Reg));

  // Notes on the sheet:
  //   To IMEM
  //   IMEM (do **NOT** move this)
  //   From IMEM
  //   Inputs/Outputs for testing. Do **NOT** move these.
  //   To DMEM
  //   DMEM (do **NOT** move this)
  //   From DMEM
endmodule
